// Logisim project Questao1.circ as structural Verilog: 1 circuit, main circuit main
module main (
  input  EO,
  input  LOAD,
  input  CLR_ASC,
  input  D0,
  input  D1,
  input  D2,
  input  D3,
  output Q0,
  output Q1,
  output Q2,
  output Q3
);

  wire and_1_out, and_3_out, and_4_out, and_6_out, and_7_out, and_10_out, and_11_out, and_12_out,
       clock_1_out, d_ff_1_q, d_ff_2_q, d_ff_3_q, d_ff_4_q, not_1_out, not_2_out, not_3_out, not_4_out,
       or_1_out, or_2_out, or_3_out, or_4_out;

  Clock clock_1 (.out(clock_1_out));
  and and_1 (and_1_out, D0, LOAD);
  and and_2 (Q0, EO, d_ff_1_q);
  D_Flip_Flop #(.Pre_Clr_Positions("LEGACY"), .enable("true"), .NewFFLayout("false")) d_ff_1 (
    .clk(clock_1_out), .D(D0), .Q(d_ff_1_q), .preset(and_1_out), .reset(or_1_out));  // open: Qn, en
  or or_1 (or_1_out, CLR_ASC, and_4_out);
  and and_3 (and_3_out, D1, LOAD);
  and and_4 (and_4_out, LOAD, not_1_out);
  not not_1 (not_1_out, D0);
  and and_5 (Q1, EO, d_ff_2_q);
  D_Flip_Flop #(.Pre_Clr_Positions("LEGACY"), .enable("true"), .NewFFLayout("false")) d_ff_2 (
    .clk(clock_1_out), .D(D1), .Q(d_ff_2_q), .preset(and_3_out), .reset(or_2_out));  // open: Qn, en
  or or_2 (or_2_out, CLR_ASC, and_7_out);
  and and_6 (and_6_out, D2, LOAD);
  and and_7 (and_7_out, LOAD, not_2_out);
  not not_2 (not_2_out, D1);
  and and_8 (Q3, EO, d_ff_4_q);
  and and_9 (Q2, EO, d_ff_3_q);
  D_Flip_Flop #(.Pre_Clr_Positions("LEGACY"), .enable("true"), .NewFFLayout("false")) d_ff_3 (
    .clk(clock_1_out), .D(D2), .Q(d_ff_3_q), .preset(and_6_out), .reset(or_3_out));  // open: Qn, en
  or or_3 (or_3_out, CLR_ASC, and_11_out);
  and and_10 (and_10_out, D3, LOAD);
  and and_11 (and_11_out, LOAD, not_3_out);
  not not_3 (not_3_out, D2);
  D_Flip_Flop #(.Pre_Clr_Positions("LEGACY"), .enable("true"), .NewFFLayout("false")) d_ff_4 (
    .clk(clock_1_out), .D(D3), .Q(d_ff_4_q), .preset(and_10_out), .reset(or_4_out));  // open: Qn, en
  or or_4 (or_4_out, CLR_ASC, and_12_out);
  and and_12 (and_12_out, LOAD, not_4_out);
  not not_4 (not_4_out, D3);
endmodule
