// Logisim project Questao6.circ as structural Verilog: 1 circuit, main circuit main
module main (
  input  D
);

  wire clock_1_out, t_ff_1_q, xor_1_out;

  Clock clock_1 (.out(clock_1_out));
  xor xor_1 (xor_1_out, t_ff_1_q, D);
  T_Flip_Flop t_ff_1 (.clk(clock_1_out), .T(xor_1_out), .Q(t_ff_1_q));  // open: Qn, preset, reset, en
endmodule
