// Logisim project Questao7.2.circ as structural Verilog: 1 circuit, main circuit main
module main (
);

  wire and_1_out, and_2_out, clock_1_out, t_ff_1_qn, t_ff_2_qn, t_ff_3_qn;

  Clock clock_1 (.out(clock_1_out));
  T_Flip_Flop t_ff_1 (.clk(clock_1_out), .T(1'b1), .Qn(t_ff_1_qn));  // open: Q, preset, reset
  T_Flip_Flop t_ff_2 (.clk(clock_1_out), .T(t_ff_1_qn), .Qn(t_ff_2_qn));  // open: Q, preset, reset
  and and_1 (and_1_out, t_ff_2_qn, t_ff_1_qn);
  T_Flip_Flop t_ff_3 (.clk(clock_1_out), .T(and_1_out), .Qn(t_ff_3_qn));  // open: Q, preset, reset
  and and_2 (and_2_out, t_ff_3_qn, and_1_out);
  T_Flip_Flop t_ff_4 (.clk(clock_1_out), .T(and_2_out));  // open: Q, Qn, preset, reset
endmodule
