// Logisim project Questão3.circ as structural Verilog: 1 circuit, main circuit main
module main (
  input  Inicio
);

  wire clock_1_out, d_ff_1_q, d_ff_2_q, d_ff_3_q, d_ff_4_q;

  Clock clock_1 (.out(clock_1_out));
  D_Flip_Flop d_ff_1 (.clk(clock_1_out), .D(d_ff_4_q), .Q(d_ff_1_q), .preset(Inicio));  // open: Qn, en, reset
  D_Flip_Flop d_ff_2 (.clk(clock_1_out), .D(d_ff_1_q), .Q(d_ff_2_q), .reset(Inicio));  // open: Qn, preset, en
  D_Flip_Flop d_ff_3 (.clk(clock_1_out), .D(d_ff_2_q), .Q(d_ff_3_q), .reset(Inicio));  // open: Qn, preset, en
  D_Flip_Flop d_ff_4 (.clk(clock_1_out), .D(d_ff_3_q), .Q(d_ff_4_q), .reset(Inicio));  // open: Qn, preset, en
endmodule
