// Logisim project Questão7-Evolution.circ as structural Verilog: 1 circuit, main circuit main
module main (
  output out_1,
  output out_2,
  output out_3,
  output out_4
);

  wire and_1_out, and_2_out, clock_1_out, t_ff_1_q, t_ff_2_q, t_ff_3_q;

  Clock clock_1 (.out(clock_1_out));
  T_Flip_Flop t_ff_1 (.T(1'b1), .clk(clock_1_out), .Q(t_ff_1_q), .Qn(out_1));  // open: reset, preset
  T_Flip_Flop t_ff_2 (.T(t_ff_1_q), .clk(clock_1_out), .Q(t_ff_2_q), .Qn(out_2));  // open: reset, preset
  and and_1 (and_1_out, t_ff_1_q, t_ff_2_q);
  T_Flip_Flop t_ff_3 (.T(and_1_out), .clk(clock_1_out), .Q(t_ff_3_q), .Qn(out_3));  // open: reset, preset
  and and_2 (and_2_out, and_1_out, t_ff_3_q);
  T_Flip_Flop t_ff_4 (.T(and_2_out), .clk(clock_1_out), .Qn(out_4));  // open: Q, reset, preset
endmodule
