// Logisim project Questao10.circ as structural Verilog: 1 circuit, main circuit main
module main (
  input  Inicio,
  output Q3,
  output Q2,
  output Q1,
  output Q0
);

  wire clock_1_out;

  Clock clock_1 (.out(clock_1_out));
  J_K_Flip_Flop j_k_ff_1 (.J(Q1), .clk(clock_1_out), .K(Q0), .Q(Q3), .Qn(Q2), .reset(Inicio));  // open: preset, en
  J_K_Flip_Flop j_k_ff_2 (.J(Q2), .clk(clock_1_out), .K(Q3), .Q(Q1), .Qn(Q0), .reset(Inicio));  // open: preset, en

  // Notes on the sheet:
  //   Estado 1 - 0101
  //   Estado 2 - 0110
  //   Estado 3 - 1010
  //   Estado 4 - 1001
endmodule
