// Logisim project Questao5.circ as structural Verilog: 1 circuit, main circuit main
module main (
  input  T
);

  wire clock_1_out, d_ff_1_q, xor_1_out;

  Clock clock_1 (.out(clock_1_out));
  xor xor_1 (xor_1_out, T, d_ff_1_q);
  D_Flip_Flop d_ff_1 (.clk(clock_1_out), .D(xor_1_out), .Q(d_ff_1_q));  // open: Qn, preset, en, reset
endmodule
