// Logisim project Questao9.circ as structural Verilog: 1 circuit, main circuit main
module main (
  input  Inicio
);

  wire clock_1_out, d_ff_1_qn, d_ff_4_q;

  Clock clock_1 (.out(clock_1_out));
  D_Flip_Flop d_ff_1 (.clk(clock_1_out), .D(d_ff_4_q), .Qn(d_ff_1_qn), .preset(Inicio));  // open: Q, en, reset
  D_Flip_Flop d_ff_2 (.clk(clock_1_out), .D(d_ff_4_q), .preset(Inicio));  // open: Q, Qn, en, reset
  D_Flip_Flop d_ff_3 (.clk(clock_1_out), .D(d_ff_1_qn), .preset(Inicio));  // open: Q, Qn, en, reset
  D_Flip_Flop d_ff_4 (.clk(clock_1_out), .D(d_ff_1_qn), .Q(d_ff_4_q), .preset(Inicio));  // open: Qn, en, reset

  // Notes on the sheet:
  //   D0 = Q3'
  //   D1 = Q3'
  //   D2 = Q0
  //   D3 = Q0
endmodule
