// Logisim project Questão 2.circ as structural Verilog: 1 circuit, main circuit main
module main (
  input  Enable_Output,
  input  Enable_Clock,
  input  Load,
  input  D0,
  input  D1,
  input  D2,
  input  D3,
  output Q0,
  output Q1,
  output Q2,
  output Q3
);

  wire and_1_out, and_3_out, and_5_out, and_6_out, and_7_out, and_8_out, and_10_out, and_11_out, and_13_out,
       and_14_out, clock_1_out, not_1_out, not_2_out, not_3_out, not_4_out, t_ff_1_q, t_ff_2_q, t_ff_3_q,
       t_ff_4_q;

  Clock clock_1 (.out(clock_1_out));
  and and_1 (and_1_out, Load, D0);
  and and_2 (Q0, Enable_Output, t_ff_1_q);
  T_Flip_Flop t_ff_1 (
    .clk(clock_1_out), .T(1'b1), .Q(t_ff_1_q), .preset(and_1_out), .reset(and_3_out), .en(Enable_Clock));  // open: Qn
  and and_3 (and_3_out, Load, not_1_out);
  not not_1 (not_1_out, D0);
  and and_4 (Q1, Enable_Output, t_ff_2_q);
  T_Flip_Flop t_ff_2 (
    .clk(clock_1_out), .T(t_ff_1_q), .Q(t_ff_2_q), .preset(and_6_out), .reset(and_5_out), .en(Enable_Clock));  // open: Qn
  and and_5 (and_5_out, Load, not_2_out);
  and and_6 (and_6_out, Load, D1);
  not not_2 (not_2_out, D1);
  and and_7 (and_7_out, t_ff_1_q, t_ff_2_q);
  and and_8 (and_8_out, Load, D2);
  and and_9 (Q2, Enable_Output, t_ff_3_q);
  and and_10 (and_10_out, and_7_out, t_ff_3_q);
  T_Flip_Flop t_ff_3 (
    .clk(clock_1_out), .T(and_7_out), .Q(t_ff_3_q), .preset(and_8_out), .reset(and_11_out), .en(Enable_Clock));  // open: Qn
  and and_11 (and_11_out, Load, not_3_out);
  not not_3 (not_3_out, D2);
  and and_12 (Q3, Enable_Output, t_ff_4_q);
  T_Flip_Flop t_ff_4 (
    .clk(clock_1_out), .T(and_10_out), .Q(t_ff_4_q), .preset(and_14_out), .reset(and_13_out),
    .en(Enable_Clock));  // open: Qn
  and and_13 (and_13_out, Load, not_4_out);
  and and_14 (and_14_out, Load, D3);
  not not_4 (not_4_out, D3);
endmodule
