// Logisim project Questão7.circ as structural Verilog: 1 circuit, main circuit main
module main (
  output Q0,
  output Q1,
  output Q2,
  output Q3
);

  wire and_1_out, and_2_out, clock_1_out, t_ff_1_q, t_ff_2_q, t_ff_3_q;

  Clock clock_1 (.out(clock_1_out));
  T_Flip_Flop t_ff_1 (.T(1'b1), .clk(clock_1_out), .Q(t_ff_1_q), .Qn(Q0));  // open: reset, preset
  T_Flip_Flop t_ff_2 (.T(t_ff_1_q), .clk(clock_1_out), .Q(t_ff_2_q), .Qn(Q1));  // open: reset, preset
  and and_1 (and_1_out, t_ff_1_q, t_ff_2_q);
  T_Flip_Flop t_ff_3 (.T(and_1_out), .clk(clock_1_out), .Q(t_ff_3_q), .Qn(Q2));  // open: reset, preset
  and and_2 (and_2_out, and_1_out, t_ff_3_q);
  T_Flip_Flop t_ff_4 (.T(and_2_out), .clk(clock_1_out), .Qn(Q3));  // open: Q, reset, preset
endmodule
